// Logisim project find-plantilla.circ as structural Verilog: 1 circuit, main circuit find
module find (
  input  start,
  input  [3:0] pat,
  input  [31:0] x,
  output found,
  output rdy
);

  wire clk_out, comparator_2_eq, or_1_out;
  wire [3:0] RPAT_q;
  wire [31:0] multiplexer_1_out, RX_q, shifter_1_out;

  Clock clk (.out(clk_out));
  Register #(.width(4), .trigger("falling")) RPAT (.D(pat), .en(start), .Q(RPAT_q), .clk(clk_out));  // open: clr
  or or_1 (or_1_out, start, ~found);  // OR_Gate
  Multiplexer #(.width(32), .enable("false")) multiplexer_1 (
    .in0(shifter_1_out), .in1(x), .out(multiplexer_1_out), .sel(start));
  Register #(.width(32), .trigger("falling")) RX (
    .D(multiplexer_1_out), .en(or_1_out), .Q(RX_q), .clk(clk_out));  // open: clr
  Shifter #(.width(32), .shift("lr")) shifter_1 (.in(RX_q), .\dist (5'b00001), .out(shifter_1_out));
  Comparator #(.width(4)) comparator_1 (.a(RPAT_q), .b(RX_q[3:0]), .eq(found));  // open: gt, lt
  Comparator #(.width(32)) comparator_2 (.a(RX_q), .b({32{1'b0}}), .eq(comparator_2_eq));  // open: gt, lt
  or or_2 (rdy, found, comparator_2_eq);
  // NOT_Gate not_1 is placed but not wired

  // Notes on the sheet:
  //   el caso de borde en el que no funciona es por ejemplo si el patron era 0001 y X era 111...111, ya que antes de que se cumpla X=0
  //   va a pasar por X=000..0001 por como funciona el shift, y ahí entregaría found=1 siendo que no estaba en el numero original
  //   (ya no alcanzo a arreglarlo u.u)
endmodule
