// Logisim project t1.circ as structural Verilog: 2 circuits, main circuit main
// start
module main (
  input  start,
  input  x,
  input  y,
  output eq,
  output lt
);

  wire clk_out, combinacional_d0, combinacional_d1, q0_q, q1_q;

  Clock clk (.out(clk_out));
  combinacional combinacional (
    .q1(q1_q), .q0(q0_q), .start(start), .x(x), .y(y), .eq(eq), .lt(lt), .d1(combinacional_d1),
    .d0(combinacional_d0));
  D_Flip_Flop #(.trigger("falling")) q0 (.clk(clk_out), .D(combinacional_d0), .Q(q0_q));  // open: Qn, preset, en, reset
  D_Flip_Flop #(.trigger("falling")) q1 (.clk(clk_out), .D(combinacional_d1), .Q(q1_q));  // open: Qn, preset, en, reset
  // AND_Gate and_1 is placed but not wired
  // AND_Gate and_2 is placed but not wired
endmodule

module combinacional (
  input  q1,
  input  q0,
  input  start,
  input  x,
  input  y,
  output eq,
  output lt,
  output d1,
  output d0
);

  wire and_1_out, and_2_out, and_3_out, and_4_out, and_5_out, not_1_out, not_2_out, not_3_out;

  not not_1 (not_1_out, start);
  not not_2 (not_2_out, x);
  not not_3 (not_3_out, y);
  and and_1 (and_1_out, q1, not_2_out, not_3_out);
  and and_2 (and_2_out, q1, x, y);
  and and_3 (and_3_out, not_1_out, not_2_out, y);
  and and_4 (and_4_out, q0, not_1_out, not_2_out);
  and and_5 (and_5_out, q0, not_1_out, y);
  or or_1 (d1, start, and_1_out, and_2_out);
  or or_2 (d0, and_3_out, and_4_out, and_5_out);

  assign eq = q1;
  assign lt = q0;
endmodule
