// Logisim project t2.circ as structural Verilog
module count (
  input  clk,
  input  reset,
  output leido,
  output [7:0] test
);

  Shift_Register #(.trigger("falling")) shift_register_1 (
    .in(1'b1), .clk(clk), .clr(reset), .q0(test[7]), .q1(test[6]), .q2(test[5]), .q3(test[4]), .q4(test[3]),
    .q5(test[2]), .q6(test[1]), .q7(leido));  // open: shift, out, load, d0, d1, d2, d3, d4, d5, d6, d7

  assign test[0] = leido;
endmodule

module main (
  input  in,
  output rdy,
  output [7:0] d7_d0,
  output [7:0] estado_del_shift
);

  wire and_1_out, clk_out, count_1_leido, lag_q, leido_q, not_1_out, not_2_out;
  wire [7:0] calc_1_y0;

  Clock clk (.out(clk_out));
  count count_1 (.clk(clk_out), .reset(and_1_out), .leido(count_1_leido), .test(estado_del_shift));
  and and_1 (and_1_out, leido_q, not_1_out);
  not not_1 (not_1_out, in);
  calc calc_1 (
    .in(in), .x0(d7_d0[0]), .x1(d7_d0[1]), .x2(d7_d0[2]), .x3(d7_d0[3]), .x4(d7_d0[4]), .x5(d7_d0[5]),
    .x6(d7_d0[6]), .y0(calc_1_y0[0]), .y1(calc_1_y0[1]), .y2(calc_1_y0[2]), .y3(calc_1_y0[3]),
    .y4(calc_1_y0[4]), .y5(calc_1_y0[5]), .y6(calc_1_y0[6]), .y7(calc_1_y0[7]));
  not not_2 (not_2_out, count_1_leido);
  Register #(.trigger("falling")) numero (.D(calc_1_y0), .en(not_2_out), .Q(d7_d0), .clk(clk_out));  // open: clr
  Register #(.width(1), .trigger("falling")) lag (.D(count_1_leido), .Q(lag_q), .clk(clk_out));  // open: en, clr
  Register #(.width(1), .trigger("falling")) leido (.D(count_1_leido), .Q(leido_q), .clk(clk_out));  // open: en, clr
  or or_1 (rdy, lag_q, count_1_leido);

  // Notes on the sheet:
  //   supuesto: la condición inicial del circuito no es importante (y no importa el valor de D7-D0 o RDY antes)
  //   la simulación inicia mientras se lee un dato, pero después de ese primer input todo funciona bien :)
endmodule

module calc (
  input  in,
  input  x0,
  input  x1,
  input  x2,
  input  x3,
  input  x4,
  input  x5,
  input  x6,
  output y0,
  output y1,
  output y2,
  output y3,
  output y4,
  output y5,
  output y6,
  output y7
);


  assign y0 = in;
  assign y1 = x0;
  assign y2 = x1;
  assign y3 = x2;
  assign y4 = x3;
  assign y5 = x4;
  assign y6 = x5;
  assign y7 = x6;
endmodule
